# Fritzing sketch arduino (saved by Fritzing 0.9.3b)
breadboards: 1

parts:
  Part1 = Arduino Uno (Rev3)
  Part2 = Adafruit Bluefruit LE SPI Friend [part_number="Adafruit #2633"]
  DHT1 = DHT22 Humidity and Temperature Sensor
  R1 = Resistor [tolerance=±5% resistance=220 package=THT]

nets:
  N1: Part1.D8, Part2.CS
  N2: Part1.D11_PWM/MOSI, Part2.MOSI
  N3: Part1.D12/MISO, Part2.MISO
  N4: Part1.D13/SCK, Part2.SCK
  GND: Part1.GND, Part2.GND, DHT1.GND
  N5: Part1.D2, DHT1.DATA, R1.Pin_1
  N6: Part1.D4, Part2.RST
  N7: Part1.D7, Part2.IRQ
  5V: Part1.5V, Part2.VIN, DHT1.VDD, R1.Pin_0

custom parts:
  Adafruit Bluefruit LE SPI Friend: The Bluefruit LE SPI Friend makes it easy to add Bluetooth Low Energy connectivity to anything with 4 or 5 GPIO pins. With SPI, you don't have to worry about baud rates, flow control, or giving up a hardware UART port. Connect to your Arduino or other microcontroller using the common four-pin SPI interface (MISO, MOSI, SCK and CS) plus a 5th GPIO pin for interrupts (to let the Arduino know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
